# Fritzing sketch project (saved by Fritzing 0.9.0b)
breadboards: 2

parts:
  Part1 = Arduino Mega 2560 (Rev3)
  LCD1 = LCD screen
  U1 = POT [package=alps_pot]
  J1 = Piezo Speaker

nets:
  N1: Part1.D13_PWM, J1.pin2
  N2: Part1.D9_PWM, LCD1.DB7
  N3: Part1.D8_PWM, LCD1.DB6
  5V: Part1.5V, LCD1.VDD, LCD1.LED+, U1.E
  GND: Part1.GND, LCD1.VSS, LCD1.R/W, LCD1.LED-, U1.A, J1.pin1
  N4: Part1.D4_PWM, LCD1.RS
  N5: Part1.D5_PWM, LCD1.E
  N6: Part1.D6_PWM, LCD1.DB4
  N7: Part1.D7_PWM, LCD1.DB5
  N8: LCD1.V0, U1.S
