# Fritzing sketch final Sketch (saved by Fritzing 0.9.0b)

parts:
  Part1 = Arduino Ethernet Shield (Rev3)  # not connected
  Part2 = Arduino Prototyping Shield
  J1 = Basic Servo
  J2 = Basic Servo
  J3 = Infrared Proximity Sensor
  J4 = Infrared Proximity Sensor
  J5 = Infrared Proximity Sensor
  J6 = Infrared Proximity Sensor

nets:
  N1: Part2.D7, J6.Vout
  N2: Part2.D8, J5.Vout
  N3: Part2.D12, Part2.N$235, J3.Vout
  N4: Part2.D13, J4.Vout
  GND: Part2.N$96, Part2.N$189, Part2.N$191, Part2.N$192, Part2.N$245, Part2.N$246, Part2.N$247, Part2.N$410, Part2.N$416, Part2.N$417, Part2.N$418, Part2.N$419, Part2.N$420, Part2.N$421, Part2.N$422, Part2.N$423, Part2.N$424, Part2.N$425, J2.gnd, J3.GND, J5.GND
  VCC: Part2.N$108, Part2.N$123, Part2.N$201, Part2.N$203, Part2.N$248, Part2.N$249, Part2.N$426, Part2.N$427, Part2.N$428, Part2.N$429, Part2.N$430, Part2.N$431, Part2.N$432, Part2.N$433, Part2.N$434, Part2.N$435, Part2.N$436, J1.vcc, J2.vcc, J3.Vcc, J4.Vcc
